// Digital circuit 01-register-74173.dig as structural Verilog
module _01_register_74173 (
  input  in_1,
  input  in_3,
  input  in_4,
  input  in_5,
  input  in_6,
  input  in_7,
  input  in_8,
  input  in_9,
  output out_2,
  output out_10,
  output out_11,
  output out_12
);

  _74173 _74173_1 (
    .pin1(in_1), .pin2(in_1), .pin3(out_2), .pin4(out_12), .pin5(out_11), .pin6(out_10), .pin7(in_5),
    .pin8(1'b0), .pin9(in_6), .pin10(in_6), .pin11(in_7), .pin12(in_8), .pin13(in_9), .pin14(in_3),
    .pin15(in_4), .pin16(1'b1));
endmodule
