// Digital circuit 02-8bit-register.dig as structural Verilog
module _02_8bit_register (
  input  D0,
  input  D1,
  input  D2,
  input  D3,
  input  D4,
  input  D5,
  input  D6,
  input  D7,
  input  CLK,
  input  DE,
  input  RES,
  input  OE,
  output Q0,
  output Q1,
  output Q2,
  output Q3,
  output Q4,
  output Q5,
  output Q6,
  output Q7
);

  _74173 _74173_1 (
    .pin1(OE), .pin2(OE), .pin3(Q0), .pin4(Q1), .pin5(Q2), .pin6(Q3), .pin7(CLK), .pin8(1'b0), .pin9(DE),
    .pin10(DE), .pin11(D3), .pin12(D2), .pin13(D1), .pin14(D0), .pin15(RES), .pin16(1'b1));
  _74173 _74173_2 (
    .pin1(OE), .pin2(OE), .pin3(Q4), .pin4(Q5), .pin5(Q6), .pin6(Q7), .pin7(CLK), .pin8(1'b0), .pin9(DE),
    .pin10(DE), .pin11(D7), .pin12(D6), .pin13(D5), .pin14(D4), .pin15(RES), .pin16(1'b1));

  // Notes on the sheet:
  //   Q0: pin 11
  //   D0: pin 1
  //   D1: pin 2
  //   D2: pin 3
  //   D3: pin 4
  //   Q1: pin 12
  //   Q2: pin 13
  //   D4: pin 5
  //   D5: pin 6
  //   D6: pin 7
  //   D7: pin 8
  //   CLK: pin 10
  //   Q3: pin 14
  //   Q4: pin 15
  //   Q5: pin 16
  //   Q6: pin 17
  //   Q7: pin 18
  //   DE: pin 9
  //   RES: pin 20
  //   OE: pin 19
endmodule
