// Digital circuit 03-icpu.dig as structural Verilog
module _03_icpu (
);

  wire undriven, undriven_2, undriven_3, undriven_4, undriven_5, undriven_6, undriven_7, undriven_8;

  _02_8bit_register _02_8bit_register_1 ();  // open: Q0, D0, D1, D2, D3, Q1, Q2, D4, D5, D6, D7, CLK, Q3, Q4, Q5, Q6, Q7, DE, RES, OE
  LED _7 (.in(undriven));
  LED _6 (.in(undriven_2));
  LED _5 (.in(undriven_3));
  LED _4 (.in(undriven_4));
  LED _3 (.in(undriven_5));
  LED _2 (.in(undriven_6));
  LED _1 (.in(undriven_7));
  LED _0 (.in(undriven_8));
  _02_8bit_register _02_8bit_register_2 ();  // open: Q0, D0, D1, D2, D3, Q1, Q2, D4, D5, D6, D7, CLK, Q3, Q4, Q5, Q6, Q7, DE, RES, OE
endmodule
