// Digital circuit 04-icpu-input.dig as structural Verilog
module _04_icpu_input (
  input  CLOCK,
  input  in_2,
  input  in_3,
  input  in_4,
  input  in_5,
  input  in_6,
  input  in_7,
  input  in_8,
  input  in_9,
  input  in_10,
  input  BIE,
  input  BOE,
  input  AIE,
  input  AOE,
  input  RST,
  input  IOE,
  input  in_17,
  input  _0,
  input  _1,
  input  _2,
  input  _3,
  input  _4,
  input  _5,
  input  _6,
  input  _7
);

  wire _02_register_1_p5, _02_register_1_p7, _02_register_1_p9, _02_register_1_p11, _02_register_1_p13,
       _02_register_1_p15, _02_register_1_p17, _02_register_1_p19, AIE_t, AOE_t, BIE_t, BOE_t, IN_IOE;

  not not_1 (IN_IOE, IOE);
  // _02_register _02_register_1: pin names not known; wires that end beside it: CLOCK, RST, AIE_t, AOE_t, _02_register_1_p5, _02_register_1_p5, _02_register_1_p7, _02_register_1_p7, _02_register_1_p9, _02_register_1_p9, _02_register_1_p11, _02_register_1_p11, _02_register_1_p13, _02_register_1_p13, _02_register_1_p15, _02_register_1_p15, _02_register_1_p17, _02_register_1_p17, _02_register_1_p19, _02_register_1_p19
  LED u__7 (.in(_02_register_1_p5));
  LED u__6 (.in(_02_register_1_p7));
  LED u__5 (.in(_02_register_1_p9));
  LED u__4 (.in(_02_register_1_p11));
  LED u__3 (.in(_02_register_1_p13));
  LED u__2 (.in(_02_register_1_p15));
  LED u__1 (.in(_02_register_1_p17));
  not not_2 (BOE_t, BOE);
  not not_3 (BIE_t, BIE);
  LED u__0 (.in(_02_register_1_p19));
  not not_4 (AOE_t, AOE);
  not not_5 (AIE_t, AIE);
  _74245 _74245_1 (
    .pin1(1'b1), .pin2(_7), .pin3(_6), .pin4(_5), .pin5(_4), .pin6(_3), .pin7(_2), .pin8(_1), .pin9(_0),
    .pin10(1'b0), .pin11(_02_register_1_p19), .pin12(_02_register_1_p17), .pin13(_02_register_1_p15),
    .pin14(_02_register_1_p13), .pin15(_02_register_1_p11), .pin16(_02_register_1_p9),
    .pin17(_02_register_1_p7), .pin18(_02_register_1_p5), .pin19(IN_IOE), .pin20(1'b1));
  // _02_register _02_register_2: pin names not known; wires that end beside it: _02_register_1_p19, _02_register_1_p19, _02_register_1_p17, _02_register_1_p17, _02_register_1_p15, _02_register_1_p15, _02_register_1_p13, _02_register_1_p13, _02_register_1_p11, _02_register_1_p11, _02_register_1_p9, _02_register_1_p9, _02_register_1_p7, _02_register_1_p7, _02_register_1_p5, _02_register_1_p5, BOE_t, BIE_t, RST, CLOCK

  // Other names for the same wires on the sheet: CLK = CLOCK

  // Notes on the sheet:
  //   Register A
  //   Register B
endmodule
