// Digital circuit 08-icpu-pc.dig as structural Verilog
module _08_icpu_pc (
  input  CLOCK,
  input  ROE,
  input  RAIE,
  input  PCCE,
  input  PCOE,
  input  JMP,
  input  in_7,
  input  in_8,
  input  in_9,
  input  in_10,
  input  BIE,
  input  BOE,
  input  AIE,
  input  AOE,
  input  RST,
  input  IOE,
  input  RWE,
  input  _0,
  input  _1,
  input  _2,
  input  _3,
  input  _4,
  input  _5,
  input  _6,
  input  _7
);

  wire _02_register_1_p1, _02_register_1_p2, _02_register_1_p3, _02_register_1_p4, _02_register_1_p5,
       _02_register_1_p6, _02_register_1_p7, _02_register_1_p8, AIE_t, AOE_t, BIE_t, BOE_t, ERR, IN_IOE,
       JMP_t, nor_1_out, PCOE_t, RAIE_t, ROE_t, RST_t, RWE_t;
  wire [7:0] _02_register_1_p11, RAM_d;

  // _02_register _02_register_1: pin names not known; wires that end beside it: _02_register_1_p1, _02_register_1_p2, _02_register_1_p3, _02_register_1_p4, _02_register_1_p5, _02_register_1_p6, _02_register_1_p7, _02_register_1_p8, RAIE_t, CLOCK, _02_register_1_p11[0], _02_register_1_p11[1], _02_register_1_p11[2], _02_register_1_p11[3], _02_register_1_p11[4], _02_register_1_p11[5], _02_register_1_p11[6], _02_register_1_p11[7], 1'b0, RST
  RAMSinglePortSel #(.AddrBits(8), .Bits(8)) RAM (
    .A(_02_register_1_p11), .CS(~1'b0), .WE(~RWE_t), .OE(~ROE_t), .D(RAM_d));
  nor nor_1 (nor_1_out, 1'b0, ~RWE_t, ROE_t);  // NOr
  not not_1 (IN_IOE, IOE);
  not not_2 (RWE_t, RWE);
  not not_3 (RAIE_t, RAIE);
  // _02_register _02_register_2: pin names not known; wires that end beside it: CLOCK, RST, AIE_t, AOE_t, _02_register_1_p8, _02_register_1_p8, _02_register_1_p7, _02_register_1_p7, _02_register_1_p6, _02_register_1_p6, _02_register_1_p5, _02_register_1_p5, _02_register_1_p4, _02_register_1_p4, _02_register_1_p3, _02_register_1_p3, _02_register_1_p2, _02_register_1_p2, _02_register_1_p1, _02_register_1_p1
  BusSplitter #(.Bits(8)) bussplitter_1 (
    .D(RAM_d), .OE(nor_1_out), .D0(_02_register_1_p1), .D1(_02_register_1_p2), .D2(_02_register_1_p3),
    .D3(_02_register_1_p4), .D4(_02_register_1_p5), .D5(_02_register_1_p6), .D6(_02_register_1_p7),
    .D7(_02_register_1_p8));
  not not_4 (ROE_t, ROE);
  LED u__7 (.in(_02_register_1_p8));
  not not_5 (PCOE_t, PCOE);
  not not_6 (JMP_t, JMP);
  LED u__6 (.in(_02_register_1_p7));
  LED u__5 (.in(_02_register_1_p6));
  LED u__4 (.in(_02_register_1_p5));
  LED u__3 (.in(_02_register_1_p4));
  LED u__2 (.in(_02_register_1_p3));
  LED u__1 (.in(_02_register_1_p2));
  not not_7 (BOE_t, BOE);
  not not_8 (BIE_t, BIE);
  LED u__0 (.in(_02_register_1_p1));
  not not_9 (AOE_t, AOE);
  not not_10 (AIE_t, AIE);
  _74245 _74245_1 (
    .pin1(1'b1), .pin2(_7), .pin3(_6), .pin4(_5), .pin5(_4), .pin6(_3), .pin7(_2), .pin8(_1), .pin9(_0),
    .pin10(1'b0), .pin11(_02_register_1_p1), .pin12(_02_register_1_p2), .pin13(_02_register_1_p3),
    .pin14(_02_register_1_p4), .pin15(_02_register_1_p5), .pin16(_02_register_1_p6),
    .pin17(_02_register_1_p7), .pin18(_02_register_1_p8), .pin19(IN_IOE), .pin20(1'b1));
  // _02_register _02_register_3: pin names not known; wires that end beside it: _02_register_1_p1, _02_register_1_p1, _02_register_1_p2, _02_register_1_p2, _02_register_1_p3, _02_register_1_p3, _02_register_1_p4, _02_register_1_p4, _02_register_1_p5, _02_register_1_p5, _02_register_1_p6, _02_register_1_p6, _02_register_1_p7, _02_register_1_p7, _02_register_1_p8, _02_register_1_p8, BOE_t, BIE_t, RST, CLOCK
  _07_program_counter _07_program_counter_1 (
    .D0(_02_register_1_p1), .D1(_02_register_1_p2), .D2(_02_register_1_p3), .D3(_02_register_1_p4),
    .D4(_02_register_1_p5), .D5(_02_register_1_p6), .D6(_02_register_1_p7), .D7(_02_register_1_p8),
    .Q1(_02_register_1_p2), .Q2(_02_register_1_p3), .Q3(_02_register_1_p4), .Q0(_02_register_1_p1),
    .Q5(_02_register_1_p6), .Q6(_02_register_1_p7), .Q7(_02_register_1_p8), .Q4(_02_register_1_p5),
    .RST(RST_t), .JMP(JMP_t), .PCCE(PCCE), .ERR(ERR), .CLK(CLOCK), .PCOE(PCOE_t));
  not not_11 (RST_t, RST);
  LED led_1 (.in(ERR));

  // Other names for the same wires on the sheet: CLK = CLOCK

  // Notes on the sheet:
  //   Register A
  //   Register B
endmodule
