// Digital circuit 11-icpu-conntroller-2.dig as structural Verilog
module _11_icpu_conntroller_2 (
  input  CLOCK,
  input  RST,
  input  _0,
  input  _1,
  input  _2,
  input  _3,
  input  _4,
  input  _5,
  input  _6,
  input  _7
);

  wire _74161_1_pin3, _74161_1_pin4, _74161_1_pin5, _74161_1_pin6, AI, AIE, AO, AOE, BI, BIE, BO, BOE, CE,
       CO, CODEI, ERR, IN_IOE, IO, IRCI, IRO, IRRI, JMP, JUMP, MI, nor_1_out, not_1_out, PCOE, RAIE, RANDI,
       RANDO, RO, ROE, RST_t, RW, RWE;
  wire [1:0] eeprom_1_d;
  wire [3:0] _02_register_1_p2, _02_register_1_p7, _74161_1_pin14;
  wire [7:0] _02_register_1_p11, DEBUG_IROPCODE, RAM_d;

  not not_1 (not_1_out, CLOCK);
  _74161 _74161_1 (
    .pin1(1'b1), .pin2(not_1_out), .pin3(_74161_1_pin3), .pin4(_74161_1_pin4), .pin5(_74161_1_pin5),
    .pin6(_74161_1_pin6), .pin7(1'b1), .pin8(1'b0), .pin9(1'b1), .pin10(1'b1), .pin11(_74161_1_pin14[3]),
    .pin12(_74161_1_pin14[2]), .pin13(_74161_1_pin14[1]), .pin14(_74161_1_pin14[0]), .pin16(1'b1));  // open: pin15
  // NotConnected on _74161_1_pin3
  // NotConnected on _74161_1_pin4
  // NotConnected on _74161_1_pin5
  // NotConnected on _74161_1_pin6
  EEPROM #(.AddrBits(4), .Bits(16)) eeprom_1 (
    .A(_74161_1_pin14), .CS(~1'b0), .WE(~1'b1), .OE(~1'b0),
    .D({IO, MI, RW, RO, CO, CE, JUMP, CODEI, RANDI, RANDO, eeprom_1_d, BI, BO, AI, AO}));
  Seven_Seg_Hex seven_seg_hex_1 (.d({IO, MI, RW, RO}), .dp(1'b0));
  LED led_1 (.in(eeprom_1_d[1]));
  LED led_2 (.in(eeprom_1_d[0]));
  Seven_Seg_Hex seven_seg_hex_2 (.d({CO, CE, JUMP, CODEI}), .dp(1'b0));
  Seven_Seg_Hex seven_seg_hex_3 (.d({RANDI, RANDO, eeprom_1_d}), .dp(1'b0));
  Seven_Seg_Hex seven_seg_hex_4 (.d({BI, BO, AI, AO}), .dp(1'b0));
  Seven_Seg_Hex seven_seg_hex_5 (.d(DEBUG_IROPCODE[7:4]), .dp(1'b0));
  // _02_register _02_register_1: pin names not known; wires that end beside it: _02_register_1_p2[0], _02_register_1_p2[1], _02_register_1_p2[2], _02_register_1_p2[3], _02_register_1_p7[0], _02_register_1_p7[1], _02_register_1_p7[2], _02_register_1_p7[3], RAIE, CLOCK, _02_register_1_p11[0], _02_register_1_p11[1], _02_register_1_p11[2], _02_register_1_p11[3], _02_register_1_p11[4], _02_register_1_p11[5], _02_register_1_p11[6], _02_register_1_p11[7], 1'b0, RST
  Seven_Seg_Hex seven_seg_hex_6 (.d(DEBUG_IROPCODE[3:0]), .dp(1'b0));
  // _02_register _02_register_2: pin names not known; wires that end beside it: DEBUG_IROPCODE[7], DEBUG_IROPCODE[7], _02_register_1_p7[3], DEBUG_IROPCODE[6], DEBUG_IROPCODE[6], _02_register_1_p7[2], DEBUG_IROPCODE[5], DEBUG_IROPCODE[5], _02_register_1_p7[1], DEBUG_IROPCODE[4], DEBUG_IROPCODE[4], _02_register_1_p7[0], DEBUG_IROPCODE[3], DEBUG_IROPCODE[3], _02_register_1_p2[3], DEBUG_IROPCODE[2], DEBUG_IROPCODE[2], _02_register_1_p2[2]
  // _02_register _02_register_3: pin names not known; wires that end beside it: DEBUG_IROPCODE[1], DEBUG_IROPCODE[1], _02_register_1_p2[1], DEBUG_IROPCODE[0], DEBUG_IROPCODE[0], _02_register_1_p2[0], 1'b0, IRCI, RST, CLOCK, _02_register_1_p7[3], _02_register_1_p7[3], _02_register_1_p7[2], _02_register_1_p7[2], _02_register_1_p7[1], _02_register_1_p7[1], _02_register_1_p7[0], _02_register_1_p7[0], _02_register_1_p2[3], _02_register_1_p2[3], _02_register_1_p2[2], _02_register_1_p2[2], _02_register_1_p2[1], _02_register_1_p2[1], _02_register_1_p2[0], _02_register_1_p2[0], IRO, IRRI, RST, CLOCK
  RAMSinglePortSel #(.AddrBits(8), .isProgramMemory("true"), .Bits(8)) RAM (
    .A(_02_register_1_p11), .CS(~1'b0), .WE(~RWE), .OE(~ROE), .D(RAM_d));
  nor nor_1 (nor_1_out, 1'b0, ~RWE, ROE);  // NOr
  not not_2 (IN_IOE, IO);
  not not_3 (RWE, RW);
  not not_4 (RAIE, MI);
  // _02_register _02_register_4: pin names not known; wires that end beside it: CLOCK, RST, AIE, AOE, _02_register_1_p7[3], _02_register_1_p7[3], _02_register_1_p7[2], _02_register_1_p7[2], _02_register_1_p7[1], _02_register_1_p7[1], _02_register_1_p7[0], _02_register_1_p7[0], _02_register_1_p2[3], _02_register_1_p2[3], _02_register_1_p2[2], _02_register_1_p2[2], _02_register_1_p2[1], _02_register_1_p2[1], _02_register_1_p2[0], _02_register_1_p2[0]
  BusSplitter #(.Bits(8)) bussplitter_1 (
    .D(RAM_d), .OE(nor_1_out), .D0(_02_register_1_p2[0]), .D1(_02_register_1_p2[1]),
    .D2(_02_register_1_p2[2]), .D3(_02_register_1_p2[3]), .D4(_02_register_1_p7[0]),
    .D5(_02_register_1_p7[1]), .D6(_02_register_1_p7[2]), .D7(_02_register_1_p7[3]));
  not not_5 (ROE, RO);
  not not_6 (PCOE, CO);
  LED u__7 (.in(_02_register_1_p7[3]));
  not not_7 (JMP, JUMP);
  LED u__6 (.in(_02_register_1_p7[2]));
  LED u__5 (.in(_02_register_1_p7[1]));
  not not_8 (IRCI, CODEI);
  not not_9 (IRRI, RANDI);
  LED u__4 (.in(_02_register_1_p7[0]));
  LED u__3 (.in(_02_register_1_p2[3]));
  not not_10 (IRO, RANDO);
  LED u__2 (.in(_02_register_1_p2[2]));
  LED u__1 (.in(_02_register_1_p2[1]));
  not not_11 (BIE, BI);
  LED u__0 (.in(_02_register_1_p2[0]));
  not not_12 (AIE, AI);
  not not_13 (BOE, BO);
  Seven_Seg_Hex seven_seg_hex_7 (.d(_02_register_1_p7), .dp(1'b0));
  not not_14 (AOE, AO);
  Seven_Seg_Hex seven_seg_hex_8 (.d(_02_register_1_p2), .dp(1'b0));
  _74245 _74245_1 (
    .pin1(1'b1), .pin2(_7), .pin3(_6), .pin4(_5), .pin5(_4), .pin6(_3), .pin7(_2), .pin8(_1), .pin9(_0),
    .pin10(1'b0), .pin11(_02_register_1_p2[0]), .pin12(_02_register_1_p2[1]), .pin13(_02_register_1_p2[2]),
    .pin14(_02_register_1_p2[3]), .pin15(_02_register_1_p7[0]), .pin16(_02_register_1_p7[1]),
    .pin17(_02_register_1_p7[2]), .pin18(_02_register_1_p7[3]), .pin19(IN_IOE), .pin20(1'b1));
  // _02_register _02_register_5: pin names not known; wires that end beside it: _02_register_1_p2[0], _02_register_1_p2[0], _02_register_1_p2[1], _02_register_1_p2[1], _02_register_1_p2[2], _02_register_1_p2[2], _02_register_1_p2[3], _02_register_1_p2[3], _02_register_1_p7[0], _02_register_1_p7[0], _02_register_1_p7[1], _02_register_1_p7[1], _02_register_1_p7[2], _02_register_1_p7[2], _02_register_1_p7[3], _02_register_1_p7[3], BOE, BIE, RST, CLOCK
  _07_program_counter _07_program_counter_1 (
    .D0(_02_register_1_p2[0]), .D1(_02_register_1_p2[1]), .D2(_02_register_1_p2[2]),
    .D3(_02_register_1_p2[3]), .D4(_02_register_1_p7[0]), .D5(_02_register_1_p7[1]),
    .D6(_02_register_1_p7[2]), .D7(_02_register_1_p7[3]), .Q1(_02_register_1_p2[1]),
    .Q2(_02_register_1_p2[2]), .Q3(_02_register_1_p2[3]), .Q0(_02_register_1_p2[0]),
    .Q5(_02_register_1_p7[1]), .Q6(_02_register_1_p7[2]), .Q7(_02_register_1_p7[3]),
    .Q4(_02_register_1_p7[0]), .RST(RST_t), .JMP(JMP), .PCCE(CE), .ERR(ERR), .CLK(CLOCK), .PCOE(PCOE));
  not not_15 (RST_t, RST);
  LED led_3 (.in(ERR));
  Seven_Seg_Hex seven_seg_hex_9 (.d(DEBUG_IROPCODE[3:0]), .dp(1'b0));
  Seven_Seg_Hex seven_seg_hex_10 (.d(DEBUG_IROPCODE[7:4]), .dp(1'b0));

  // Other names for the same wires on the sheet: PCCE = CE; CLK = CLOCK

  // Notes on the sheet:
  //   CLOCK: Hz: 2
  //   contents of eeprom_1 (hex, n*v repeats v):
  //   4800,1500,4800,1480,42,1
  //   Register A
  //   Register B
endmodule
